# Fritzing sketch JuliannaClarke_assign5 (saved by Fritzing 0.9.3b)
breadboards: 1

parts:
  Part1 = Arduino Uno (Rev3)
  LED2 = LED - 5mm [color="Red (633nm)" package="5 mm [THT]"]
  R2 = Resistor [tolerance=±5% resistance=560 package=THT]
  LED3 = LED - 5mm [color="Red (633nm)" package="5 mm [THT]"]
  R3 = Resistor [tolerance=±5% resistance=560 package=THT]
  LED5 = LED - 5mm [color="Red (633nm)" package="5 mm [THT]"]
  R5 = Resistor [tolerance=±5% resistance=560 package=THT]
  S1 = Pushbutton [package="[THT]"]
  R7 = Resistor [tolerance=±5% resistance=10k package=THT]
  R8 = Photocell (LDR) [package=THT]
  R9 = Resistor [tolerance=±5% resistance=10k package=THT]

nets:
  N1: Part1.A0, R8.pin_1, R9.Pin_0
  N2: Part1.D8, S1.Pin_1, S1.Pin_2, R7.Pin_0
  N3: Part1.D3_PWM, LED5.anode
  N4: Part1.D5_PWM, LED3.anode
  N5: Part1.D6_PWM, LED2.anode
  N6: Part1.5V, S1.Pin_3, S1.Pin_4, R8.pin_0
  N7: Part1.GND, R2.Pin_1, R3.Pin_1, R5.Pin_1, R7.Pin_1, R9.Pin_1
  N8: LED2.cathode, R2.Pin_0
  N9: LED3.cathode, R3.Pin_0
  N10: LED5.cathode, R5.Pin_0

notes:
  Assignment #1
  Note: The button can be wired without +5V and pulldown resistor using INPUT_PULLUP. How would it change?

// code stored in the sketch: assignment1.ino
/*
 **********************************************************************************************************************************
 * Assignment 1
 * (Author), Sept 2015
 * 
 * Description:
 * 
 * Circuit:
 *  LEDs on digital pins 2-7 (remember resistors)
 * a push button on digital 8
 * a potentiometer on analog input 5
 *
 * Software Requirements:
 * Create at least 3 animation sequences for the LEDs.
 * Use the push button to toggle between the animation sequences.
 * Use the potentiometer to control an aspect of each animation (speed, brightness, etc.)
 *
 * Things to keep in mind:
 * 	  Try to avoid using delay()
 *    clearly comment code
 *    If you collaborate, always include the names of collaborators
 *
 *  BONUS: try using some PWM in your LED sequences
 *  SUPER BONUS: Route PCB to two layers ready for fab
 *
 *  Behavior:
 *  (Please describe expected output here) 
 **********************************************************************************************************************************
 */

// Hardware definitions  ///////////////////////////////////////////////
const int LED_COUNT = 6;
int ledPins[] = {2,3,4,5,6,7};
const int potPin = A5;
const int buttonPin = 8;

// System Code ////////////////////////////////////////////////////////
void setup() {  
  // Initialize Hardware 
  Serial.begin(9600); 
  Serial.println("Running Assignment 1");
  Serial.println("Author, Date");
  
  // initialize the LEDs as outputs

  // init button

  // Run tests
  Serial.println("*** Press the button to run the animations... ***");
}

void loop() {
}
